# Fritzing sketch TinySound (saved by Fritzing 0.9.2b)
circuit board: 3cm x 3cm
breadboards: 1

parts:
  ATTiny85 = attiny85 [package=dip]
  Audio_Jack = 3.5mm Audio Jack [package=audio-jack]
  Battery = LIPO-110mAh [package=lipo-110]
  Switch = Pushbutton [package="[THT]"]

nets:
  N1: ATTiny85.Pin_2, Switch.Pin_3, Switch.Pin_4
  N2: ATTiny85.Pin_3, Audio_Jack.SLEEVE
  N3: ATTiny85.Pin_4, Battery.-, Switch.Pin_1, Switch.Pin_2
  N4: ATTiny85.Pin_6, Audio_Jack.RIGHT, Audio_Jack.LEFT
  N5: ATTiny85.Pin_8, Battery.+
